// Logisim project Atv 2-a.circ as structural Verilog: 1 circuit, main circuit main
module main (
  input  W,
  input  X,
  input  Y,
  input  Z,
  input  S1,
  input  S0,
  output out_7
);

  wire and_1_out, and_2_out, and_3_out, and_4_out;

  and and_1 (and_1_out, W, ~S1, ~S0);  // AND_Gate
  and and_2 (and_2_out, X, ~S1, S0);  // AND_Gate
  and and_3 (and_3_out, Y, S1, ~S0);  // AND_Gate
  and and_4 (and_4_out, Z, S1, S0);
  or M (out_7, and_1_out, and_2_out, and_3_out, and_4_out);

  // Notes on the sheet:
  //   MULTIPLEXADOR 4 PORTAS
endmodule
