// Logisim project Atv 2-b.circ as structural Verilog: 1 circuit, main circuit main
module main (
  input  A0,
  input  A1,
  input  A2,
  input  A3,
  input  B0,
  input  B1,
  input  B2,
  input  B3,
  input  T,
  input  Binv,
  output S0,
  output S1,
  output S2,
  output S3,
  output OverF
);

  wire and_1_out, and_2_out, and_3_out, and_4_out, and_5_out, and_6_out, and_7_out, and_8_out, or_1_out,
       or_2_out, or_3_out, or_4_out, or_5_out, or_6_out, or_7_out, xor_1_out, xor_2_out, xor_4_out,
       xor_5_out, xor_7_out, xor_8_out, xor_10_out, xor_11_out;

  or or_1 (or_1_out, T, B0);
  xor xor_1 (xor_1_out, A0, B0);
  and and_1 (and_1_out, T, B0);
  xor xor_2 (xor_2_out, A0, Binv);
  xor xor_3 (S0, xor_1_out, T);
  and and_2 (and_2_out, xor_2_out, or_1_out);
  or or_2 (or_2_out, and_1_out, and_2_out);
  xor xor_4 (xor_4_out, A1, B1);
  and and_3 (and_3_out, or_2_out, B1);
  xor xor_5 (xor_5_out, A1, Binv);
  or or_3 (or_3_out, or_2_out, B1);
  xor xor_6 (S1, xor_4_out, or_2_out);
  and and_4 (and_4_out, xor_5_out, or_3_out);
  or or_4 (or_4_out, and_3_out, and_4_out);
  or or_5 (or_5_out, or_4_out, B2);
  xor xor_7 (xor_7_out, A2, B2);
  and and_5 (and_5_out, or_4_out, B2);
  xor xor_8 (xor_8_out, A2, Binv);
  xor xor_9 (S2, xor_7_out, or_4_out);
  and and_6 (and_6_out, xor_8_out, or_5_out);
  or or_6 (or_6_out, and_5_out, and_6_out);
  xor xor_10 (xor_10_out, A3, B3);
  and and_7 (and_7_out, or_6_out, B3);
  xor xor_11 (xor_11_out, A3, Binv);
  or or_7 (or_7_out, or_6_out, B3);
  xor xor_12 (S3, xor_10_out, or_6_out);
  and and_8 (and_8_out, xor_11_out, or_7_out);
  or or_8 (OverF, and_7_out, and_8_out);

  // Notes on the sheet:
  //   SOMADOR SUBTRATOR
endmodule
